// Logisim project tisc.circ as structural Verilog
module main (
  input  in_1,
  input  in_2
);

  wire and_1_out, CLK, CLKRAW, IP_regp_enable, not_1_out, RegEnable, RegReset, RegWriteEnable;
  wire [1:0] ALU_OP2;
  wire [2:0] RegSelect, RegSelect2;
  wire [7:0] InstData_high8, InstData_low8, IP_low8, RegData8, RegData8_1, RegData8_2, RegOut8, RegOut8_2;

  Clock clock_1 (.out(CLKRAW));
  not not_1 (not_1_out, in_1);
  and and_1 (and_1_out, CLKRAW, not_1_out);
  or or_1 (CLK, and_1_out, in_2);
  IP_reg_enable ip_reg_enable_1 (
    .enable(IP_regp_enable), .RegSelect(RegSelect), .RegEnable(RegEnable), .IP_low_sel(RegSelect2),
    .WriteEnable(RegWriteEnable));
  registers registers_1 (
    .Enable(RegEnable), .RegSelect3_1(RegSelect), .IP_low_8(IP_low8), .Data8(RegData8),
    .WriteEnable(RegWriteEnable), .CLK(CLK), .Reset(RegReset), .RegSelect3_2(RegSelect2),
    .StdOut8_1(RegOut8), .StdOut8_2(RegOut8_2));
  IP_inc ip_inc_1 (
    .RegBus8(RegOut8), .IP_low(RegOut8_2), .inc_high(InstData_high8), .inc_low(InstData_low8),
    .IP_low8(IP_low8), .Reg_IP_high8(RegData8_1));
  assign RegData8 = RegData8_1 | RegData8_2;  // OR_Gate or_2, 8 bits wide
  ALU alu_1 (
    .PrimaryOperand(RegOut8), .SecondaryOperand(RegOut8_2), .ALUOpcode2(ALU_OP2), .CLK(CLK),
    .out_5(RegData8_2));

  // Other names for the same wires on the sheet: CLKHLDHIGH = in_2; CLKHLDLOW = in_1; RegEnable_1 = RegEnable;
  //   RegSelect2_1[2:0] = RegSelect2; RegSelect_1[2:0] = RegSelect; RegWriteEnable_1 = RegWriteEnable

  // Notes on the sheet:
  //   To make 
  //   Add access to IP_low
endmodule

module ALU (
  input  [7:0] PrimaryOperand,
  input  [7:0] SecondaryOperand,
  input  [1:0] ALUOpcode2,
  input  CLK,
  output [7:0] out_5
);

  wire [7:0] adder_1_out, multiplexer_1_out, nand_1_out, subtractor_1_out;

  Adder adder_1 (.a(PrimaryOperand), .b(SecondaryOperand), .out(adder_1_out));  // open: cin, cout
  Subtractor subtractor_1 (.a(PrimaryOperand), .b(SecondaryOperand), .out(subtractor_1_out));  // open: bin, bout
  assign nand_1_out = ~(PrimaryOperand & SecondaryOperand);  // NAND_Gate nand_1, 8 bits wide
  Multiplexer #(.select(2), .width(8)) multiplexer_1 (
    .in0(adder_1_out), .in1(subtractor_1_out), .in2(nand_1_out), .in3(SecondaryOperand),
    .out(multiplexer_1_out), .sel(ALUOpcode2));
  Register #(.trigger("high")) Temp (.D(multiplexer_1_out), .en(1'b1), .clk(CLK), .Q(out_5));  // open: clr

  // Notes on the sheet:
  //   High Level as registers are falling egde
endmodule

module IP_inc (
  input  [7:0] RegBus8,
  input  [7:0] IP_low,
  input  [7:0] inc_high,
  input  [7:0] inc_low,
  output [7:0] IP_low8,
  output [7:0] Reg_IP_high8
);

  wire adder_1_cout;

  Adder adder_1 (.a(IP_low), .b(inc_low), .out(IP_low8), .cout(adder_1_cout));  // open: cin
  Adder adder_2 (.a(inc_high), .b(RegBus8), .out(Reg_IP_high8), .cin(adder_1_cout));  // open: cout
endmodule

module IP_reg_enable (
  input  enable,
  output [2:0] RegSelect,
  output RegEnable,
  output [2:0] IP_low_sel,
  output WriteEnable
);

  assign {IP_low_sel[2:1], RegSelect[0]} = {{2{enable}}, enable};  // Bit_Extender bit_extender_1
  not not_1 (IP_low_sel[0], RegSelect[0]);

  assign RegEnable = enable;
  assign RegSelect[2:1] = IP_low_sel[2:1];
  assign WriteEnable = enable;
endmodule

module registers (
  input  Enable,
  input  [2:0] RegSelect3_1,
  input  [7:0] IP_low_8,
  input  [7:0] Data8,
  input  WriteEnable,
  input  CLK,
  input  Reset,
  input  [2:0] RegSelect3_2,
  output [7:0] StdOut8_1,
  output [7:0] StdOut8_2
);

  wire and_1_out, decoder_1_out0, decoder_1_out1, decoder_1_out2, decoder_1_out3, decoder_1_out4,
       decoder_1_out5, decoder_1_out6, decoder_1_out7, not_1_out, or_1_out;
  wire [7:0] IP_high_out8, IP_high_rawout8, IP_low_out8, IP_low_rawout8, multiplexer_2_out,
       multiplexer_3_out, ret_high_reg_out8, ret_high_reg_rawout8, ret_low_reg_out8, ret_low_reg_rawout8,
       wreg_out8, wreg_rawout8, xreg_out8, xreg_rawout8, yreg_out8, yreg_rawout8, zreg_out8, zreg_rawout8;

  Multiplexer #(.select(3), .width(8)) multiplexer_1 (
    .in0(xreg_rawout8), .in1(yreg_rawout8), .in2(zreg_rawout8), .in3(wreg_rawout8),
    .in4(ret_low_reg_rawout8), .in5(ret_high_reg_rawout8), .in6(IP_low_rawout8), .in7(IP_high_rawout8),
    .out(StdOut8_2), .sel(RegSelect3_2));
  Decoder #(.select(3)) decoder_1 (
    .out0(decoder_1_out0), .out1(decoder_1_out1), .out2(decoder_1_out2), .out3(decoder_1_out3),
    .out4(decoder_1_out4), .out5(decoder_1_out5), .out6(decoder_1_out6), .out7(decoder_1_out7),
    .sel(RegSelect3_1), .en(Enable));
  reg_simplified xreg (
    .WriteEnable(WriteEnable), .CLK(CLK), .Data8(Data8), .Enable(decoder_1_out0), .Reset(Reset),
    .RawOut8(xreg_rawout8), .Out8(xreg_out8));
  reg_simplified yreg (
    .WriteEnable(WriteEnable), .CLK(CLK), .Data8(Data8), .Enable(decoder_1_out1), .Reset(Reset),
    .RawOut8(yreg_rawout8), .Out8(yreg_out8));
  reg_simplified zreg (
    .WriteEnable(WriteEnable), .CLK(CLK), .Data8(Data8), .Enable(decoder_1_out2), .Reset(Reset),
    .RawOut8(zreg_rawout8), .Out8(zreg_out8));
  reg_simplified wreg (
    .WriteEnable(WriteEnable), .CLK(CLK), .Data8(Data8), .Enable(decoder_1_out3), .Reset(Reset),
    .RawOut8(wreg_rawout8), .Out8(wreg_out8));
  reg_simplified IP_high (
    .WriteEnable(WriteEnable), .CLK(CLK), .Data8(Data8), .Enable(decoder_1_out7), .Reset(Reset),
    .RawOut8(IP_high_rawout8), .Out8(IP_high_out8));
  reg_simplified IP_low (
    .WriteEnable(WriteEnable), .CLK(CLK), .Data8(multiplexer_2_out), .Enable(or_1_out), .Reset(Reset),
    .RawOut8(IP_low_rawout8), .Out8(IP_low_out8));
  reg_simplified ret_high_reg (
    .WriteEnable(WriteEnable), .CLK(CLK), .Data8(Data8), .Enable(decoder_1_out5), .Reset(Reset),
    .RawOut8(ret_high_reg_rawout8), .Out8(ret_high_reg_out8));
  reg_simplified ret_low_reg (
    .WriteEnable(WriteEnable), .CLK(CLK), .Data8(Data8), .Enable(decoder_1_out4), .Reset(Reset),
    .RawOut8(ret_low_reg_rawout8), .Out8(ret_low_reg_out8));
  or or_1 (or_1_out, decoder_1_out6, and_1_out);
  Multiplexer #(.width(8)) multiplexer_2 (.in0(Data8), .in1(IP_low_8), .out(multiplexer_2_out), .sel(and_1_out));
  not not_1 (not_1_out, RegSelect3_2[0]);
  and and_1 (and_1_out, not_1_out, RegSelect3_2[1], RegSelect3_2[2]);
  Multiplexer #(.width(8)) multiplexer_3 (
    .in0({8{1'b0}}), .in1(IP_low_out8), .out(multiplexer_3_out), .sel(decoder_1_out6));
  assign StdOut8_1 = IP_high_out8 | multiplexer_3_out | ret_high_reg_out8 | ret_low_reg_out8 | wreg_out8 | zreg_out8 | yreg_out8 | xreg_out8;  // OR_Gate or_2, 8 bits wide
endmodule

module reg_simplified (
  input  [7:0] Data8,
  input  WriteEnable,
  input  CLK,
  input  Enable,
  input  Reset,
  output [7:0] RawOut8,
  output [7:0] Out8
);

  wire and_1_out, and_3_out;
  wire [7:0] bit_extender_1_out;

  and and_1 (and_1_out, WriteEnable, Enable);
  Register #(.trigger("falling")) Reg8 (.D(Data8), .en(and_1_out), .clk(CLK), .Q(RawOut8), .clr(and_3_out));
  assign bit_extender_1_out = {{7{Enable}}, Enable};  // Bit_Extender bit_extender_1
  assign Out8 = RawOut8 & bit_extender_1_out;  // AND_Gate and_2, 8 bits wide
  and and_3 (and_3_out, Enable, Reset);
endmodule

module Serial_Shift_Reg (
  input  [7:0] DATA8IN,
  input  Enable,
  input  DATAREADY_CLK,
  input  READ_N,
  output [7:0] Data8Late,
  output [7:0] Data8Early,
  output CLKHLDLOW
);

  wire and_1_out, and_2_out, and_3_out, d_ff_1_q, d_ff_2_q, not_1_out, not_2_out, not_3_out, not_4_out,
       not_5_out;

  not not_1 (not_1_out, DATAREADY_CLK);
  not not_2 (not_2_out, not_1_out);
  not not_3 (not_3_out, not_2_out);
  and and_1 (and_1_out, not_3_out, DATAREADY_CLK);
  and and_2 (and_2_out, Enable, and_1_out);
  and and_3 (and_3_out, DATAREADY_CLK, not_5_out);
  D_Flip_Flop d_ff_1 (.D(1'b1), .clk(and_3_out), .Q(d_ff_1_q), .reset(and_2_out));  // open: Qn, preset
  Register register_1 (.D(DATA8IN), .en(1'b1), .clk(and_3_out), .Q(Data8Late));  // open: clr
  not not_4 (not_4_out, READ_N);
  Register register_2 (.D(Data8Late), .en(1'b1), .clk(and_3_out), .Q(Data8Early));  // open: clr
  D_Flip_Flop d_ff_2 (.D(d_ff_1_q), .clk(and_3_out), .Q(d_ff_2_q), .reset(and_2_out));  // open: Qn, preset
  not not_5 (not_5_out, CLKHLDLOW);
  Multiplexer multiplexer_1 (.in0(d_ff_2_q), .in1(d_ff_1_q), .out(CLKHLDLOW), .sel(not_4_out));
endmodule
